# Fritzing sketch fritzing (saved by Fritzing 0.9.3b)
perfboards: 1

parts:
  Gizwits_WiFi_Witty_ESP-12F1 = Gizwits WiFi Witty ESP-12F
  S1 = Pushbutton [package="[THT]"]
  S2 = Pushbutton [package="[THT]"]
  J2 = female pin header, 8 pins [form="♀ (female)"]
  J3 = female pin header, 8 pins [form="♀ (female)"]
  J4 = female pin header, 5 pins [form="♀ (female)"]
  J1 = female pin header, 3 pins [form="♀ (female)"]
  R2 = Resistor [tolerance=±5% resistance=10k package=THT]
  J5 = female pin header, 4 pins [form="♀ (female)"]
  R3 = Resistor [tolerance=±5% resistance=2.2k package=THT]
  R4 = Resistor [tolerance=±5% resistance=2.2k package=THT]
  R5 = Resistor [tolerance=±5% resistance=2.2k package=THT]
  R1 = Resistor [tolerance=±5% resistance=1k package=THT]
  C1 = Electrolytic Capacitor [capacitance=0.22mF package="100 mil [THT, electrolytic]"]
  C2 = Electrolytic Capacitor [capacitance=22µF package="100 mil [THT, electrolytic]"]

nets:
  N1: Gizwits_WiFi_Witty_ESP-12F1.REST, J2.pin8, R1.Pin_1
  N2: Gizwits_WiFi_Witty_ESP-12F1.ADC, J2.pin7
  N3: Gizwits_WiFi_Witty_ESP-12F1.CH_PD, J2.pin6
  N4: Gizwits_WiFi_Witty_ESP-12F1.GPIO16, J2.pin5
  N5: Gizwits_WiFi_Witty_ESP-12F1.GPIO14, J2.pin4
  N6: Gizwits_WiFi_Witty_ESP-12F1.GPIO12, J2.pin3, J1.pin3
  N7: Gizwits_WiFi_Witty_ESP-12F1.GPIO13, J2.pin2
  N8: Gizwits_WiFi_Witty_ESP-12F1.VCC, J2.pin1, J4.pin5, J1.pin2, J5.pin1, R3.Pin_0, C1.+, C2.+
  N9: Gizwits_WiFi_Witty_ESP-12F1.GND, S1.Pin_1, S1.Pin_2, J3.pin1, J4.pin1, J1.pin1, R2.Pin_1, J5.pin3, R5.Pin_0, C1.-, C2.-
  N10: Gizwits_WiFi_Witty_ESP-12F1.GPIO15, J3.pin2
  N11: Gizwits_WiFi_Witty_ESP-12F1.GPIO2, J3.pin3
  N12: Gizwits_WiFi_Witty_ESP-12F1.GPIO0, S2.Pin_1, S2.Pin_2, J3.pin4, R2.Pin_0
  N13: Gizwits_WiFi_Witty_ESP-12F1.GPIO4, J3.pin5
  N14: Gizwits_WiFi_Witty_ESP-12F1.GPIO5, J3.pin6
  N15: Gizwits_WiFi_Witty_ESP-12F1.RXD, J3.pin7, R4.Pin_1, R5.Pin_1
  N16: Gizwits_WiFi_Witty_ESP-12F1.TXD, J3.pin8, J5.pin4
  N17: S1.Pin_3, S1.Pin_4, R1.Pin_0
  N18: S2.Pin_3, S2.Pin_4, R3.Pin_1
  N19: J5.pin2, R4.Pin_0
